# Fritzing sketch Laser Viscometer (saved by Fritzing 0.9.3b)
breadboards: 1

parts:
  Part1 = Arduino Nano (Rev3.0)
  LD1 = LD
  LD2 = LD

nets:
  N1: Part1.D13/SCK, LD1.anode, LD2.anode
  N2: LD1.cathode, LD2.cathode

custom parts:
  LD: A Generic Red Dot Laser Diode Module (~5mW)
